// Logisim project cpu.circ as structural Verilog: 1 circuit, main circuit cpu
module cpu (
  input  clk,
  input  [31:0] INSTRUCTION,
  input  [31:0] READ_DATA,
  output [31:0] WRITE_ADDRESS,
  output [31:0] PROGRAM_COUNTER,
  output [31:0] ra,
  output [31:0] sp,
  output [31:0] t0,
  output [31:0] t1,
  output [31:0] t2,
  output [31:0] s0,
  output [31:0] s1,
  output [31:0] a0,
  output [31:0] tohost,
  output [3:0] WRITE_ENABLE,
  output [31:0] WRITE_DATA
);

  wire ASel, BrEq, BrLt, BrUn, BSel, CSRSel, CSRWen, lb, lh, MemRW, PCSel, RegWEn, sb, sh;
  wire [1:0] WBSel;
  wire [2:0] funct3, ImmSel;
  wire [3:0] ALUSel, multiplexer_7_out, multiplexer_8_out;
  wire [6:0] funct7;
  wire [24:0] INSTRUCTION_IN;
  wire [31:0] adder_1_out, adder_2_out, bit_extender_1_out, bit_extender_2_out, imm, multiplexer_1_out,
       multiplexer_2_out, multiplexer_3_out, multiplexer_4_out, multiplexer_6_out, multiplexer_10_out,
       PROGRAM_COUNTER2, READ_DATA2, rs1_data, Write_Data_t;

  Multiplexer #(.enable("false"), .width(32)) multiplexer_1 (
    .in0(adder_1_out), .in1(WRITE_ADDRESS), .out(multiplexer_1_out), .sel(PCSel));
  Adder #(.width(32)) adder_1 (.a(PROGRAM_COUNTER), .b(32'h4), .out(adder_1_out));  // open: cin, cout
  Register #(.width(32)) PC (.D(multiplexer_1_out), .clk(clk), .Q(PROGRAM_COUNTER));  // open: en, clr
  Multiplexer #(.enable("false"), .width(32)) multiplexer_2 (
    .in0(INSTRUCTION), .in1(32'h13), .out(multiplexer_2_out), .sel(PCSel));
  Register #(.width(32)) register_1 (
    .D(multiplexer_2_out), .clk(clk), .Q({funct7, INSTRUCTION_IN[24:15], funct3, INSTRUCTION_IN[11:0]}));  // open: en, clr
  Register #(.width(32)) register_2 (.D(PROGRAM_COUNTER), .clk(clk), .Q(PROGRAM_COUNTER2));  // open: en, clr
  control_logic control_logic_1 (
    .CSRWen(CSRWen), .lb(lb), .lh(lh), .sb(sb), .sh(sh), .PCSel(PCSel), .RegWEn(RegWEn), .ImmSel(ImmSel),
    .BrUn(BrUn), .ASel(ASel), .BSel(BSel), .ALUSel(ALUSel), .MemRW(MemRW), .WBSel(WBSel), .CSRSel(CSRSel),
    .inst({funct7, INSTRUCTION_IN[24:15], funct3, INSTRUCTION_IN[11:0]}), .BrEq(BrEq), .BrLt(BrLt));
  regfile regfile_1 (
    .rs1(INSTRUCTION_IN[19:15]), .rs2(INSTRUCTION_IN[24:20]), .rd(INSTRUCTION_IN[11:7]),
    .Write_Data(Write_Data_t), .RegWEn(RegWEn), .clk(clk), .ra(ra), .sp(sp), .t0(t0), .t1(t1), .t2(t2),
    .s0(s0), .s1(s1), .a0(a0), .Read_Data_1(rs1_data), .Read_Data_2(WRITE_DATA));
  branch_comp branch_comp_1 (.rs1(rs1_data), .rs2(WRITE_DATA), .BrUn(BrUn), .BrEq(BrEq), .BrLt(BrLt));
  imm_gen imm_gen_1 (.inst({funct7, INSTRUCTION_IN[24:15], funct3, INSTRUCTION_IN[11:0]}), .ImmSel(ImmSel), .imm(imm));
  Multiplexer #(.enable("false"), .width(32)) multiplexer_3 (
    .in0(rs1_data), .in1(PROGRAM_COUNTER2), .out(multiplexer_3_out), .sel(ASel));
  Multiplexer #(.enable("false"), .width(32)) multiplexer_4 (
    .in0(WRITE_DATA), .in1(imm), .out(multiplexer_4_out), .sel(BSel));
  Adder #(.width(32)) adder_2 (.a(PROGRAM_COUNTER2), .b(32'h4), .out(adder_2_out));  // open: cin, cout
  Multiplexer #(.enable("false"), .select(2), .width(32)) multiplexer_5 (
    .in0(READ_DATA2), .in1(WRITE_ADDRESS), .in2(adder_2_out), .in3(imm), .out(Write_Data_t), .sel(WBSel));
  alu alu_1 (.Result(WRITE_ADDRESS), .A(multiplexer_3_out), .B(multiplexer_4_out), .ALUSel(ALUSel));
  Multiplexer #(.enable("false"), .width(32)) multiplexer_6 (
    .in0(rs1_data), .in1(imm), .out(multiplexer_6_out), .sel(CSRSel));
  Multiplexer #(.enable("false"), .width(4)) multiplexer_7 (
    .in0(4'b1111), .in1(4'b0011), .out(multiplexer_7_out), .sel(sh));
  csr csr_1 (.CSR_address(12'h51e), .CSR_din(multiplexer_6_out), .CSR_WE(CSRWen), .clk(clk), .tohost(tohost));
  Multiplexer #(.enable("false"), .width(4)) multiplexer_8 (
    .in0(multiplexer_7_out), .in1(4'b0001), .out(multiplexer_8_out), .sel(sb));
  assign bit_extender_1_out = {{24{READ_DATA[7]}}, READ_DATA[7:0]};  // Bit_Extender bit_extender_1
  assign bit_extender_2_out = {{16{READ_DATA[15]}}, READ_DATA[15:0]};  // Bit_Extender bit_extender_2
  Multiplexer #(.enable("false"), .width(4)) multiplexer_9 (
    .in0(4'b0000), .in1(multiplexer_8_out), .out(WRITE_ENABLE), .sel(MemRW));
  Multiplexer #(.enable("false"), .width(32)) multiplexer_10 (
    .in0(READ_DATA), .in1(bit_extender_2_out), .out(multiplexer_10_out), .sel(lh));
  Multiplexer #(.enable("false"), .width(32)) multiplexer_11 (
    .in0(multiplexer_10_out), .in1(bit_extender_1_out), .out(READ_DATA2), .sel(lb));

  // Other names for the same wires on the sheet: ALU_Result[31:0] = WRITE_ADDRESS; opcode[6:0] = INSTRUCTION_IN[6:0];
  //   rd[4:0] = INSTRUCTION_IN[11:7]; INSTRUCTION_IN (some bits) = {funct7, funct3}; rs1[4:0] = INSTRUCTION_IN[19:15];
  //   rs2[4:0] = INSTRUCTION_IN[24:20]; rs2_data[31:0] = WRITE_DATA

  // Notes on the sheet:
  //   Output to IMEM
  //   IMEM (do **NOT** move this)
  //   Inputs from IMEM
  //   It is OK to move the PC, RegFile, ALU, MEM, Branch Comp, Imm Gen, and Control Logic to wherever is most convenient for you when constructing your CPU, and to delete this text
  //   Inputs/Outputs for testing. Do **NOT** move these.
  //   Outputs To DMEM
  //   DMEM (do **NOT** move this)
  //   Inputs From DMEM
endmodule
